# Fritzing sketch velocistamicro (saved by Fritzing 0.9.2b)
circuit board: 15.9966cm x 6.23121cm
breadboards: 1

parts:
  Parte2 = Motor Driver 1A Dual TB6612FNG
  JP1 = Header 2 [package=jst-2-pth]
  M1 = DC Motor
  M2 = DC Motor
  Parte1 = Arduino Micro (Rev3)
  U1 = PIC-ICSP-Mini [package=pic-icsp-mini]
  U2 = PIC-ICSP-Mini [package=pic-icsp-mini]
  U3 = PIC-ICSP-Mini [package=pic-icsp-mini]
  U4 = PIC-ICSP-Mini [package=pic-icsp-mini]
  M3 = DC Motor
  M4 = DC Motor
  S2 = Toggle Switch [package=THT]
  C2 = Electrolytic Capacitor [capacitance=1µF package="100 mil [THT, electrolytic]"]
  S3 = Toggle Switch [package=THT]
  S4 = Toggle Switch [package=THT]

nets:
  N1: Parte2.B01, M2.pin_1
  N2: Parte2.B02, M2.pin_2
  N3: Parte2.A02, M1.pin_1
  N4: Parte2.A01, M1.pin_2
  N5: JP1.1, S3.L1, S4.L1
  N6: JP1.2, S2.COM, C2.-
  N7: Parte1.D1/TX, M3.pin_1
  N8: Parte1.D0/RX, M3.pin_2
  N9: Parte1.GND, U2.VPP, M4.pin_2
  N10: Parte1.D2/SDA, U4.GND
  N11: Parte1.D3/SCL, U4.VCC
  N12: Parte1.D4_PWM/A6, U4.PGD
  N13: Parte1.D5_PWM, U4.VPP
  N14: Parte1.D6_PWM/A7, U1.GND
  N15: Parte1.D7, U3.VPP
  N16: Parte1.D8_PWM/A8, U3.VCC
  N17: Parte1.D9_PWM/A9, U1.VPP
  N18: Parte1.D11_PWM, U3.PGD
  N19: Parte1.D12_PWM/A11, U1.VCC
  N20: Parte1.VIN, S2.L1, C2.+
  N21: Parte1.A5, U1.PGD
  N22: Parte1.A4, U1.PGC
  N23: Parte1.A3, U2.PGC
  N24: Parte1.A2, U2.PGD
  N25: Parte1.A1, U2.GND
  N26: Parte1.A0, U2.VCC
  N27: S2.L2, S3.COM, S4.COM

notes:
  +
  en caso de analogico
