# Fritzing sketch velocistamicroVersionHiro5(VersionFinal) (Jesus) (saved by Fritzing 0.9.2b)
circuit board: 21.8997cm x 27.14cm
breadboards: 1

parts:
  JP1 = Header 2 [package=jst-2-pth]
  M3 = DC Motor
  M4 = DC Motor
  S2 = Toggle Switch [package=THT]
  C2 = Electrolytic Capacitor [capacitance=1µF package="100 mil [THT, electrolytic]"]
  S3 = Toggle Switch [package=THT]
  S4 = Toggle Switch [package=THT]
  Arduino = Arduino Micro (Rev3)

nets:
  N1: JP1.1, S3.L1, S4.L1
  N2: JP1.2, M3.pin_1, S2.COM, C2.-, Arduino.GND
  N3: M3.pin_2, Arduino.5V
  N4: M4.pin_1, Arduino.D1/TX
  N5: M4.pin_2, Arduino.D0/RX
  N6: S2.L1, C2.+, Arduino.VIN
  N7: S2.L2, S3.COM, S4.COM

notes:
  +
  GND
  OUT B
  OUT A OJO
  VCC
  M1
  M2
  OUT A
  RX
  TX
  PWM
  Sensor Distancia
  -
  VMOT
  VCC-Driver
  ojo
  ¿STBY?
